// Logisim project g2.circ as structural Verilog: 13 circuits, main circuit CPU
module _16_32_bit_extender (
  input  SignExtend,
  input  [15:0] in,
  output [31:0] out
);

  Multiplexer #(.width(32)) multiplexer_1 (
    .in0({{16{1'b0}}, in}), .in1({{17{in[15]}}, in[14:0]}), .out(out), .sel(SignExtend));
endmodule

module Control (
  input  [5:0] Instruction_input,
  output SignExtend,
  output Jump,
  output Link,
  output [11:0] Control_to_MUX
);

  PLA #(.in_width(6), .out_width(11), .truth_table("000000,00010010001#R-instructions\n001001,00101010000#addiu\n00110x,00001010000#andi/ori\n000100,00100000010#beq\n101011,00001000100#sw\n100011,00001111000#lw\n001010,00101010000#slti\n000010,01000000000#j\n000011,11010010001#jal")) pla_1 ();  // open: in, out
  // PLA #(.in_width(6), .out_width(4), .truth_table("001001,0010#addiu\n001100,0000#andi\n001101,0001#ori\n001010,0111#slti\n10x011,0010#sw og lw\n000100,0110#beq\n000011,0010#jal")) pla_2: pin names not known; wires that end beside it: Control_to_MUX[11:8]
endmodule

module ALU_Control (
  input  [3:0] immidiate_input,
  input  [5:0] funct,
  input  ALUOp_in,
  output jr,
  output [3:0] ALU_input
);

  wire [3:0] pla_1_out;

  PLA #(.in_width(6), .out_width(5), .truth_table("100001,00010#addu\n100011,00110#subu\n100100,00000#and\n100101,00001#or\n101010,00111#slt\n001000,10110#jr")) pla_1 (.out(pla_1_out));  // open: in
  Multiplexer #(.width(4)) multiplexer_1 (.in0(immidiate_input), .in1(pla_1_out), .out(ALU_input), .sel(ALUOp_in));
endmodule

module IF_ID (
  input  stall,
  input  [31:0] PC_input,
  input  [31:0] Instruction_input,
  input  Clock,
  output [31:0] PC_output,
  output [31:0] Instruction_output
);

  wire not_1_out;

  not not_1 (not_1_out, stall);
  Register #(.width(32)) register_1 (.D(PC_input), .en(not_1_out), .Q(PC_output), .clk(Clock));  // open: clr
  Register #(.width(32)) register_2 (
    .D(Instruction_input), .en(not_1_out), .Q(Instruction_output), .clk(Clock));  // open: clr
endmodule

module ID_EX (
  input  [1:0] WB_input,
  input  [1:0] M_input,
  input  [7:0] EX_input,
  input  [31:0] PC_input,
  input  [31:0] Read_Data1_input,
  input  [31:0] Read_Data2_input,
  input  [31:0] Signextend_input,
  input  [4:0] rs_input,
  input  [4:0] rt_input,
  input  [4:0] rd_input,
  input  Clock,
  output [1:0] WB_output,
  output [1:0] M_output,
  output [7:0] EX_output,
  output [31:0] PC_output,
  output [31:0] Read_Data1_output,
  output [31:0] Read_Data2_output,
  output [31:0] Signextend_output,
  output [4:0] rs_output,
  output [4:0] rt_output,
  output [4:0] rd_output
);

  Register #(.width(2)) register_1 (.D(WB_input), .Q(WB_output), .clk(Clock));  // open: en, clr
  Register #(.width(2)) register_2 (.D(M_input), .Q(M_output), .clk(Clock));  // open: en, clr
  Register register_3 (.D(EX_input), .Q(EX_output), .clk(Clock));  // open: en, clr
  Register #(.width(32)) register_4 (.D(PC_input), .Q(PC_output), .clk(Clock));  // open: en, clr
  Register #(.width(32)) register_5 (.D(Read_Data1_input), .Q(Read_Data1_output), .clk(Clock));  // open: en, clr
  Register #(.width(32)) register_6 (.D(Read_Data2_input), .Q(Read_Data2_output), .clk(Clock));  // open: en, clr
  Register #(.width(32)) register_7 (.D(Signextend_input), .Q(Signextend_output), .clk(Clock));  // open: en, clr
  Register #(.width(5)) register_8 (.D(rs_input), .Q(rs_output), .clk(Clock));  // open: en, clr
  Register #(.width(5)) register_9 (.D(rt_input), .Q(rt_output), .clk(Clock));  // open: en, clr
  Register #(.width(5)) register_10 (.D(rd_input), .Q(rd_output), .clk(Clock));  // open: en, clr
endmodule

module EX_MEM (
  input  [1:0] WB_input,
  input  [1:0] M_input,
  input  [31:0] ALU_res_input,
  input  [31:0] Read_Data2_input,
  input  [4:0] RegDst_input,
  input  Clock,
  output [1:0] WB_output,
  output [1:0] M_output,
  output [31:0] ALU_res_output,
  output [31:0] Read_Data2_output,
  output [4:0] RegDst_output
);

  Register #(.width(2)) register_1 (.D(WB_input), .Q(WB_output), .clk(Clock));  // open: en, clr
  Register #(.width(2)) register_2 (.D(M_input), .Q(M_output), .clk(Clock));  // open: en, clr
  Register #(.width(32)) register_3 (.D(ALU_res_input), .Q(ALU_res_output), .clk(Clock));  // open: en, clr
  Register #(.width(32)) register_4 (.D(Read_Data2_input), .Q(Read_Data2_output), .clk(Clock));  // open: en, clr
  Register #(.width(5)) register_5 (.D(RegDst_input), .Q(RegDst_output), .clk(Clock));  // open: en, clr
endmodule

module MEM_WB (
  input  [1:0] WB_input,
  input  [31:0] Read_Data_input,
  input  [31:0] Address_input,
  input  [4:0] RegDst_input,
  input  Clock,
  output [1:0] WB_output,
  output [31:0] Read_Data_output,
  output [31:0] Address_output,
  output [4:0] RegDst_output
);

  Register #(.width(2)) register_1 (.D(WB_input), .Q(WB_output), .clk(Clock));  // open: en, clr
  Register #(.width(32)) register_2 (.D(Read_Data_input), .Q(Read_Data_output), .clk(Clock));  // open: en, clr
  Register #(.width(32)) register_3 (.D(Address_input), .Q(Address_output), .clk(Clock));  // open: en, clr
  Register #(.width(5)) register_4 (.D(RegDst_input), .Q(RegDst_output), .clk(Clock));  // open: en, clr
endmodule

module Forwarding_unit (
  input  [4:0] EX_MEM_regdst_input,
  input  [1:0] EX_MEM_wb_input,
  input  [4:0] MEM_WB_regdts_input,
  input  [4:0] ID_EX_rs_input,
  input  [1:0] MEM_WB_wb_input,
  input  [4:0] ID_EX_rt_input,
  output [1:0] Forward_B,
  output [1:0] Forward_A
);

  EX_hazard ex_hazard_1 (
    .Forward_B(Forward_B[1]), .Forward_A(Forward_A[1]), .ID_EX_rt_input(ID_EX_rt_input),
    .EX_MEM_RegWrite(EX_MEM_wb_input[0]), .ID_EX_rs_input(ID_EX_rs_input),
    .EX_MEM_regdst_input(EX_MEM_regdst_input));
  MEM_hazard mem_hazard_1 (
    .Forward_B(Forward_B[0]), .Forward_A(Forward_A[0]), .EX_MEM_RegWrite(EX_MEM_wb_input[0]),
    .EX_MEM_regdst_input(EX_MEM_regdst_input), .ID_EX_rt_input(ID_EX_rt_input),
    .MEM_WB_RegWrite(MEM_WB_wb_input[0]), .ID_EX_rs_input(ID_EX_rs_input),
    .MEM_WB_regdst_input(MEM_WB_regdts_input));
endmodule

module equal (
  input  [4:0] in_1,
  input  [4:0] in_2,
  output out_3
);

  Comparator #(.width(5)) comparator_1 (.a(in_1), .b(in_2), .eq(out_3));  // open: gt, lt
endmodule

module EX_hazard (
  input  [4:0] ID_EX_rt_input,
  input  EX_MEM_RegWrite,
  input  [4:0] ID_EX_rs_input,
  input  [4:0] EX_MEM_regdst_input,
  output Forward_B,
  output Forward_A
);

  wire equal_1_out_3, equal_2_out_3, equal_3_out_3, not_1_out;

  and and_1 (Forward_B, EX_MEM_RegWrite, equal_1_out_3, not_1_out);
  equal equal_1 (.out_3(equal_1_out_3), .in_1(ID_EX_rt_input), .in_2(EX_MEM_regdst_input));
  and and_2 (Forward_A, EX_MEM_RegWrite, equal_2_out_3, not_1_out);
  equal equal_2 (.out_3(equal_2_out_3), .in_1(ID_EX_rs_input), .in_2(EX_MEM_regdst_input));
  not not_1 (not_1_out, equal_3_out_3);
  equal equal_3 (.out_3(equal_3_out_3), .in_1(EX_MEM_regdst_input), .in_2({5{1'b0}}));
endmodule

module MEM_hazard (
  input  EX_MEM_RegWrite,
  input  [4:0] EX_MEM_regdst_input,
  input  [4:0] ID_EX_rt_input,
  input  MEM_WB_RegWrite,
  input  [4:0] ID_EX_rs_input,
  input  [4:0] MEM_WB_regdst_input,
  output Forward_B,
  output Forward_A
);

  wire equal_1_out_3, equal_2_out_3, equal_3_out_3, ex_hazard_1_forward_a, ex_hazard_1_forward_b, not_1_out,
       not_2_out, not_3_out;

  not not_1 (not_1_out, ex_hazard_1_forward_b);
  not not_2 (not_2_out, ex_hazard_1_forward_a);
  EX_hazard ex_hazard_1 (
    .Forward_B(ex_hazard_1_forward_b), .Forward_A(ex_hazard_1_forward_a), .ID_EX_rt_input(ID_EX_rt_input),
    .EX_MEM_RegWrite(EX_MEM_RegWrite), .ID_EX_rs_input(ID_EX_rs_input),
    .EX_MEM_regdst_input(EX_MEM_regdst_input));
  and and_1 (Forward_B, not_1_out, equal_1_out_3, MEM_WB_RegWrite, not_3_out);
  equal equal_1 (.out_3(equal_1_out_3), .in_1(ID_EX_rt_input), .in_2(MEM_WB_regdst_input));
  and and_2 (Forward_A, not_2_out, equal_2_out_3, MEM_WB_RegWrite, not_3_out);
  equal equal_2 (.out_3(equal_2_out_3), .in_1(ID_EX_rs_input), .in_2(MEM_WB_regdst_input));
  not not_3 (not_3_out, equal_3_out_3);
  equal equal_3 (.out_3(equal_3_out_3), .in_1(MEM_WB_regdst_input), .in_2({5{1'b0}}));
endmodule

module Hazard_detection (
  input  ID_EX_MemRead,
  input  [4:0] ID_EX_RegisterRt,
  input  [4:0] IF_ID_RegisterRs,
  input  [4:0] IF_ID_RegisterRt,
  output stall
);

  wire equal_1_out_3, equal_2_out_3, or_1_out;

  equal equal_1 (.out_3(equal_1_out_3), .in_1(ID_EX_RegisterRt), .in_2(IF_ID_RegisterRs));
  equal equal_2 (.out_3(equal_2_out_3), .in_1(ID_EX_RegisterRt), .in_2(IF_ID_RegisterRt));
  or or_1 (or_1_out, equal_1_out_3, equal_2_out_3);
  and and_1 (stall, ID_EX_MemRead, or_1_out);
endmodule

module CPU (
);

  wire alu_control_1_jr, and_1_out, and_2_out, clock_1_out, comparator_1_eq, control_1_jump, control_1_link,
       control_1_signextend, hazard_detection_1_stall, mips_alu_1_p4, not_1_out, or_1_out, or_2_out;
  wire [1:0] ex_mem_1_m_output, ex_mem_1_wb_output, forwarding_unit_1_forward_a, forwarding_unit_1_forward_b,
       id_ex_1_m_output, id_ex_1_wb_output, registerfile_1_p3;
  wire [3:0] alu_control_1_alu_input;
  wire [4:0] ex_mem_1_regdst_output, id_ex_1_rd_output, id_ex_1_rs_output, id_ex_1_rt_output,
       multiplexer_4_out, multiplexer_5_out, multiplexer_9_out, multiplexer_10_out, registerfile_1_p4;
  wire [5:0] id_ex_1_signextend_output;
  wire [7:0] id_ex_1_ex_output;
  wire [11:0] control_1_control_to_mux, multiplexer_6_out;
  wire [27:0] if_id_1_pc_output;
  wire [31:0] adder_1_out, adder_2_out, ex_mem_1_alu_res_output, ex_mem_1_read_data2_output,
       id_ex_1_pc_output, id_ex_1_read_data1_output, id_ex_1_read_data2_output, mem_wb_1_address_output,
       mem_wb_1_read_data_output, mips_alu_1_p5, mips_ram_1_p6, mipsprogramrom_1_p2, multiplexer_1_out,
       multiplexer_2_out, multiplexer_3_out, multiplexer_7_out, multiplexer_8_out, multiplexer_11_out,
       multiplexer_12_out, multiplexer_13_out, multiplexer_14_out, n16_32_bit_extender_1_out, register_1_q,
       registerfile_1_p1, registerfile_1_p7, registerfile_1_p8, shifter_1_out;
  wire [31:2] if_id_1_instruction_output;
  wire [31:6] id_ex_1_signextend_output_2;
  wire [31:26] if_id_1_instruction_output_2;

  Multiplexer #(.width(32)) multiplexer_1 (
    .in0(multiplexer_2_out), .in1(multiplexer_14_out), .out(multiplexer_1_out), .sel(and_2_out));
  Multiplexer #(.width(32)) multiplexer_2 (
    .in0(adder_1_out), .in1({if_id_1_instruction_output, 2'b00}), .out(multiplexer_2_out),
    .sel(control_1_jump));
  Register #(.width(32)) register_1 (
    .D(multiplexer_1_out), .en(not_1_out), .Q(register_1_q), .clk(clock_1_out));  // open: clr
  not not_1 (not_1_out, hazard_detection_1_stall);
  Clock clock_1 (.out(clock_1_out));
  Adder #(.width(32)) adder_1 (.a(register_1_q), .b(32'h4), .out(adder_1_out));  // open: cin, cout
  or or_1 (or_1_out, and_2_out, control_1_jump);
  // MIPSProgramROM mipsprogramrom_1: pin names not known; wires that end beside it: register_1_q, mipsprogramrom_1_p2
  Hazard_detection hazard_detection_1 (
    .ID_EX_MemRead(id_ex_1_m_output[1]), .ID_EX_RegisterRt(id_ex_1_rt_output),
    .IF_ID_RegisterRs(if_id_1_instruction_output[27:23]),
    .IF_ID_RegisterRt(if_id_1_instruction_output[22:18]), .stall(hazard_detection_1_stall));
  IF_ID if_id_1 (
    .PC_input(adder_1_out), .Instruction_input(multiplexer_3_out), .stall(hazard_detection_1_stall),
    .Clock(clock_1_out), .PC_output({if_id_1_instruction_output[31:28], if_id_1_pc_output}),
    .Instruction_output({if_id_1_instruction_output_2, if_id_1_instruction_output[27:2]}));
  Multiplexer #(.width(32)) multiplexer_3 (
    .in0(mipsprogramrom_1_p2), .in1({32{1'b0}}), .out(multiplexer_3_out), .sel(or_1_out));
  Comparator #(.width(6)) comparator_1 (
    .a(if_id_1_instruction_output[7:2]), .b(6'b001000), .eq(comparator_1_eq));  // open: gt, lt
  Control control_1 (
    .Instruction_input(if_id_1_instruction_output_2), .SignExtend(control_1_signextend),
    .Jump(control_1_jump), .Link(control_1_link), .Control_to_MUX(control_1_control_to_mux));
  and and_1 (and_1_out, ~and_2_out, ~hazard_detection_1_stall);  // AND_Gate
  _16_32_bit_extender u_16_32_bit_extender_1 (
    .in(if_id_1_instruction_output[17:2]), .SignExtend(control_1_signextend), .out(n16_32_bit_extender_1_out));
  Multiplexer #(.width(5)) multiplexer_4 (
    .in0(if_id_1_instruction_output[22:18]), .in1({5{1'b1}}), .out(multiplexer_4_out), .sel(comparator_1_eq));
  Multiplexer #(.width(5)) multiplexer_5 (
    .in0(if_id_1_instruction_output[27:23]), .in1({5{1'b1}}), .out(multiplexer_5_out), .sel(comparator_1_eq));
  Multiplexer #(.width(12)) multiplexer_6 (
    .in0({12{1'b0}}), .in1(control_1_control_to_mux), .out(multiplexer_6_out), .sel(and_1_out));
  // RegisterFile #(.trigger("falling")) registerfile_1: pin names not known; wires that end beside it: registerfile_1_p1, clock_1_out, registerfile_1_p3[0], registerfile_1_p4, multiplexer_5_out, multiplexer_4_out, registerfile_1_p7, registerfile_1_p8
  Multiplexer #(.width(32)) multiplexer_7 (
    .in0(registerfile_1_p7), .in1({if_id_1_instruction_output[31:28], if_id_1_pc_output}),
    .out(multiplexer_7_out), .sel(control_1_link));
  Multiplexer #(.width(32)) multiplexer_8 (
    .in0(registerfile_1_p8), .in1({if_id_1_instruction_output[31:28], if_id_1_pc_output}),
    .out(multiplexer_8_out), .sel(control_1_link));
  Multiplexer #(.width(5)) multiplexer_9 (
    .in0(if_id_1_instruction_output[17:13]), .in1({5{1'b1}}), .out(multiplexer_9_out), .sel(control_1_link));
  ID_EX id_ex_1 (
    .WB_input(multiplexer_6_out[5:4]), .M_input(multiplexer_6_out[3:2]),
    .EX_input({multiplexer_6_out[11:6], multiplexer_6_out[1:0]}),
    .PC_input({if_id_1_instruction_output[31:28], if_id_1_pc_output}), .Read_Data1_input(multiplexer_7_out),
    .Read_Data2_input(multiplexer_8_out), .Signextend_input(n16_32_bit_extender_1_out),
    .rs_input(multiplexer_5_out), .rt_input(multiplexer_4_out), .rd_input(multiplexer_9_out),
    .Clock(clock_1_out), .WB_output(id_ex_1_wb_output), .M_output(id_ex_1_m_output),
    .EX_output(id_ex_1_ex_output), .PC_output(id_ex_1_pc_output),
    .Read_Data1_output(id_ex_1_read_data1_output), .Read_Data2_output(id_ex_1_read_data2_output),
    .Signextend_output({id_ex_1_signextend_output_2, id_ex_1_signextend_output}),
    .rs_output(id_ex_1_rs_output), .rt_output(id_ex_1_rt_output), .rd_output(id_ex_1_rd_output));
  ALU_Control alu_control_1 (
    .funct(id_ex_1_signextend_output), .ALUOp_in(id_ex_1_ex_output[0]),
    .immidiate_input(id_ex_1_ex_output[7:4]), .jr(alu_control_1_jr), .ALU_input(alu_control_1_alu_input));
  Multiplexer #(.width(5)) multiplexer_10 (
    .in0(id_ex_1_rt_output), .in1(id_ex_1_rd_output), .out(multiplexer_10_out), .sel(id_ex_1_ex_output[3]));
  Shifter #(.width(32)) shifter_1 (
    .in({id_ex_1_signextend_output_2, id_ex_1_signextend_output}), .\dist (5'b00010), .out(shifter_1_out));
  Multiplexer #(.select(2), .width(32)) multiplexer_11 (
    .in0(id_ex_1_read_data1_output), .in1(registerfile_1_p1), .in2(ex_mem_1_alu_res_output),
    .out(multiplexer_11_out), .sel(forwarding_unit_1_forward_a));  // open: in3
  Multiplexer #(.select(2), .width(32)) multiplexer_12 (
    .in0(id_ex_1_read_data2_output), .in1(registerfile_1_p1), .in2(ex_mem_1_alu_res_output),
    .out(multiplexer_12_out), .sel(forwarding_unit_1_forward_b));  // open: in3
  Forwarding_unit forwarding_unit_1 (
    .ID_EX_rs_input(id_ex_1_rs_output), .ID_EX_rt_input(id_ex_1_rt_output),
    .Forward_B(forwarding_unit_1_forward_b), .Forward_A(forwarding_unit_1_forward_a),
    .EX_MEM_regdst_input(ex_mem_1_regdst_output), .EX_MEM_wb_input(ex_mem_1_wb_output),
    .MEM_WB_regdts_input(registerfile_1_p4), .MEM_WB_wb_input(registerfile_1_p3));
  Adder #(.width(32)) adder_2 (.a(id_ex_1_pc_output), .b(shifter_1_out), .out(adder_2_out));  // open: cin, cout
  Multiplexer #(.width(32)) multiplexer_13 (
    .in0(multiplexer_12_out), .in1({id_ex_1_signextend_output_2, id_ex_1_signextend_output}),
    .out(multiplexer_13_out), .sel(id_ex_1_ex_output[2]));
  // Mips_ALU mips_alu_1: pin names not known; wires that end beside it: multiplexer_11_out, multiplexer_13_out, alu_control_1_alu_input, mips_alu_1_p4, mips_alu_1_p5
  or or_2 (or_2_out, alu_control_1_jr, id_ex_1_ex_output[1]);
  Multiplexer #(.width(32)) multiplexer_14 (
    .in0(adder_2_out), .in1(multiplexer_11_out), .out(multiplexer_14_out), .sel(alu_control_1_jr));
  and and_2 (and_2_out, or_2_out, mips_alu_1_p4);
  EX_MEM ex_mem_1 (
    .WB_input(id_ex_1_wb_output), .M_input(id_ex_1_m_output), .ALU_res_input(mips_alu_1_p5),
    .Read_Data2_input(id_ex_1_read_data2_output), .RegDst_input(multiplexer_10_out), .Clock(clock_1_out),
    .WB_output(ex_mem_1_wb_output), .M_output(ex_mem_1_m_output), .ALU_res_output(ex_mem_1_alu_res_output),
    .Read_Data2_output(ex_mem_1_read_data2_output), .RegDst_output(ex_mem_1_regdst_output));
  // MIPS_RAM #(.addrWidth(24)) mips_ram_1: pin names not known; wires that end beside it: ex_mem_1_alu_res_output[23:0], ex_mem_1_read_data2_output, ex_mem_1_m_output[0], ex_mem_1_m_output[1], clock_1_out, mips_ram_1_p6
  MEM_WB mem_wb_1 (
    .WB_input(ex_mem_1_wb_output), .Read_Data_input(mips_ram_1_p6), .Address_input(ex_mem_1_alu_res_output),
    .RegDst_input(ex_mem_1_regdst_output), .Clock(clock_1_out), .WB_output(registerfile_1_p3),
    .Read_Data_output(mem_wb_1_read_data_output), .Address_output(mem_wb_1_address_output),
    .RegDst_output(registerfile_1_p4));
  Multiplexer #(.width(32)) multiplexer_15 (
    .in0(mem_wb_1_address_output), .in1(mem_wb_1_read_data_output), .out(registerfile_1_p1),
    .sel(registerfile_1_p3[1]));

  // Notes on the sheet:
  //   contents of mipsprogramrom_1 (hex, n*v repeats v):
  //   jal     largest_prime           # largest_prime(28)      #      addu    $v0, $0, $0             #
  //   return 0      j       end  largest_prime:             addiu   $sp, $sp, -24           # GÃ¸r plads
  //   til 4 registre     sw      $ra, 20($sp)            # Gem retur adressen pÃ¥ stacken        sw
  //   $s4, 16($sp)            # Gem s-registrene, vi skal bruge s4 til primes         sw      $s3, 12($sp)
  //   # gem $s3 i stacken, da vi skal bruge s3 til n  sw      $s2, 8($sp)                     sw      $s1,
  //   4($sp)                     sw      $s0, 0($sp)             # vi skal bruge s0 til i        addu
  //   $s3, $a0, $0            # Gem argumentet n i s3         addiu   $a1, $0, 4              # Vi vil
  //   gange n med 4  jal     mul                     # for at fÃ¥ stÃ¸rrelsen pÃ¥ vores array        subu
  //   $sp, $sp, $v0           # Ryk stakpegeren for at gÃ¸re plads til primes         addu    $s4, $sp, $0
  //   # Gem primes i s4       addiu   $s0, $s0, 2             # i = 2 L1:     slt     $t0, $s0, $s3
  //   # t0 = i < n?   beq     $t0, $0, L1_exit        # hvis i >= n hop ud            addu    $a0, $0, $s0
  //   # find offsetet til primes[i]   addiu   $a1, $0, 4      jal     mul     addu    $t0, $v0, $s4   sw
  //   $s0, 0($t0)             # gem i i primes[i]     addiu   $s0, $s0, 1             # forÃ¸g i med 1
  //   j       L1  L1_exit:    addiu   $s1, $0, 2              # Initialiser p=2 L2:   addu    $a0, $s1, $0
  //   # GÃ¸r klar til at gange p med sig selv         addu    $a1, $a0, $0    jal     mul
  //   # v0 = p*p      slt     $t0, $v0, $s3           # SÃ¦t t0 til 1 hvis p*p er mindre end n        beq
  //   $t0, $0, L2_exit        # Hvis p*p ikke er mindre end n, forlad lÃ¸kke          addu    $a0, $s1, $0
  //   # GÃ¸r klar til at gange p med 4 (offset ind i primes)  addiu   $a1, $0, 4                      jal
  //   mul                     # v0 = p*4      addu    $t1, $v0, $s4           # t1 = offset i primes til
  //   p. primes + p*4      lw      $t0, 0($t1)             # t0 = primes[p]        beq     $t0, $0,
  //   L2_continue    # spring videre hvis primes[p] = 0      addiu   $s0, $0, 2              # i = 2  W1:
  //   addu    $a0, $s0, $0            # GÃ¸r klar til at gange i med p. a0 = i        addu    $a1, $s1, $0
  //   # a1 = p        jal     mul                             # v0 = i*p      addu    $s2, $v0, $0
  //   # idx = i*p     slt     $t0, $s2, $s3           # t0 = idx < n  beq     $t0, $0, W1_break       #
  //   break hvis idx ikke er < n, altsÃ¥ idx >= n   addu    $a0, $s2, $0            # gÃ¸r kar til at
  //   gange idx med 4 (offset ind i primes)         addiu   $a1, $0, 4      jal     mul
  //   # v0 = p*4      addu    $t0, $v0, $s4           # t0 = primes + idx*4 = positionen af primes[idx]
  //   sw      $0, 0($t0)              # primes[idx] = 0       addiu   $s0, $s0, 1             # i++   j
  //   W1       W1_break:               L2_continue:   addiu   $s1, $s1, 1             # inkrementer p
  //   j       L2  L2_exit:    addu    $s0, $s3, $0            #  i = n (vi trækker en fra på næste linje
  //   L3:  addiu   $s0, $s0, -1            # i = i - 1     slti    $t0, $s0, 2             # t0 = i < 2
  //   addiu   $t1, $0, 1              # t1 = 1        beq     $t1, $t0, L3_exit       # exit loop hvis i <
  //   2          addu    $a0, $s0, $0            # GÃ¸r klar til at regne i*4 (offset i primes til i) a0 =
  //   i     addiu   $a1, $0, 4              # a1 = 4        jal     mul                     # v0 = i*4
  //   addu    $t1, $v0, $s4           # t1 = i*4 + primes = positionen af primes[i]   lw      $t0, 0($t1)
  //   # t0 = primes[i]        beq     $t0, $0, L3             # Hvis primes[i] er nul, loop igen      j
  //   largest_prime_exit      # return i       L3_exit:               addu    $s0, $0, $0             #
  //   gÃ¸r returvÃ¦rdien klar        largest_prime_exit:    addu    $a0, $s3, $0            # GÃ¸r klar
  //   til at gange n med 4        addiu   $a1, $0, 4              # Vi vil gange n med 4  jal     mul
  //   # for at fÃ¥ stÃ¸rrelsen pÃ¥ vores array        addu    $sp, $sp, $v0           # Ryk stakpegeren
  //   for at gÃ¸re plads til primes         addu    $v0, $s0, $0            # Gem returnværdien     lw
  //   $ra, 20($sp)            # hent returadressen retur adressen pÃ¥ stacken         lw      $s4, 16($sp)
  //   # hent s-registrene ind igen    lw      $s3, 12($sp)    lw      $s2, 8($sp)             lw      $s1,
  //   4($sp)     lw      $s0, 0($sp)     addiu   $sp, $sp, 24            # GÃ¸r plads til 4 registre
  //   jr      $ra                     # skal fikses  mul:     addiu   $t1, $0, 1              # t1 = 1, vi
  //   skal bruge den til at dekrementere         addu    $v0, $0, $0             # returvÃ¦rdien
  //   initialiseres til 0      mulloop:       slti    $t0, $a1, 1             # t0 = b < 1    beq     $t0,
  //   $t1, mulexit       # Hvis b < 1 eller b !> 0, exit         subu    $a1, $a1, $t1           #
  //   dekrementer b         addu    $v0, $v0, $a0           # LÃ¦g a til resultatet         j
  //   mulloop                 # loop   mulexit:       jr      $ra                     # returner   end:
endmodule
